// Logisim project CPU_Control.circ as structural Verilog: 16 circuits, main circuit Control
module Control (
  input  [3:0] in_1,
  output out_2,
  output out_3,
  output Mem_Write,
  output Clock_Stop,
  output Write_ra,
  output Read_ra,
  output Reg_Write,
  output Branch,
  output ALU_op1,
  output ALU_op2,
  output ALU_Src,
  output out_13
);

  MemRead memread_1 (.in_1(in_1), .out_2(out_2));
  MemtoReg memtoreg_1 (.in_1(in_1), .out_2(out_3));
  MemWrite memwrite_1 (.in_1(in_1), .out_2(Mem_Write));
  clockStop clockstop_1 (.in_1(in_1), .out_2(Clock_Stop));
  writea_ra writea_ra_1 (.in_1(in_1), .out_2(Write_ra));
  Read_ra read_ra_1 (.in_1(in_1), .out_2(Read_ra));
  RegWrite regwrite_1 (.in_1(in_1), .out_2(Reg_Write));
  B_ranch b_ranch_1 (.in_1(in_1), .out_2(Branch));
  ALUop1 aluop1_1 (.in_1(in_1), .out_2(ALU_op1));
  ALUop2 aluop2_1 (.in_1(in_1), .out_2(ALU_op2));
  ALUSrc alusrc_1 (.in_1(in_1), .out_2(ALU_Src));
  regDst regdst_1 (.in_1(in_1), .out_2(out_13));
endmodule

module MemRead (
  input  [3:0] in_1,
  output out_2
);

  wire not_1_out, not_2_out, not_3_out;

  not not_1 (not_1_out, in_1[1]);
  not not_2 (not_2_out, in_1[2]);
  not not_3 (not_3_out, in_1[3]);
  and and_1 (out_2, in_1[0], not_1_out, not_2_out, not_3_out);
endmodule

// Mem_to_Reg
module MemtoReg (
  input  [3:0] in_1,
  output out_2
);

  wire not_1_out, not_2_out, not_3_out;

  not not_1 (not_1_out, in_1[1]);
  not not_2 (not_2_out, in_1[2]);
  not not_3 (not_3_out, in_1[3]);
  and and_1 (out_2, in_1[0], not_1_out, not_2_out, not_3_out);
endmodule

module MemWrite (
  input  [3:0] in_1,
  output out_2
);

  wire not_1_out, not_2_out;

  not not_1 (not_1_out, in_1[1]);
  not not_2 (not_2_out, in_1[3]);
  and and_1 (out_2, in_1[0], not_1_out, in_1[2], not_2_out);
endmodule

module clockStop (
  input  [3:0] in_1,
  output out_2
);

  and and_1 (out_2, in_1[0], in_1[1], in_1[2], in_1[3]);
endmodule

module writea_ra (
  input  [3:0] in_1,
  output out_2
);

  wire not_1_out;

  not not_1 (not_1_out, in_1[1]);
  and and_1 (out_2, in_1[0], not_1_out, in_1[2], in_1[3]);
endmodule

module Read_ra (
  input  [3:0] in_1,
  output out_2
);

  wire not_1_out;

  not not_1 (not_1_out, in_1[0]);
  and and_1 (out_2, not_1_out, in_1[1], in_1[2], in_1[3]);
endmodule

module RegWrite (
  input  [3:0] in_1,
  output out_2
);

  wire and_1_out, and_2_out, and_3_out, and_4_out;

  and and_1 (and_1_out, ~in_1[0], ~in_1[1], ~in_1[3]);  // AND_Gate
  and and_2 (and_2_out, ~in_1[3], ~in_1[2], ~in_1[1]);  // AND_Gate
  and and_3 (and_3_out, in_1[3], ~in_1[2], ~in_1[1]);  // AND_Gate
  buf and_4 (and_4_out, ~in_1[1]);  // AND_Gate AND_Gate
  or or_1 (out_2, and_1_out, and_2_out, and_3_out, and_4_out);
endmodule

module B_ranch (
  input  [3:0] in_1,
  output out_2
);

  wire and_1_out, and_2_out, and_3_out, and_4_out;

  and and_1 (and_1_out, in_1[2], ~in_1[1], ~in_1[0]);  // AND_Gate
  and and_2 (and_2_out, ~in_1[1], in_1[2], in_1[3]);  // AND_Gate
  and and_3 (and_3_out, in_1[1], ~in_1[2], in_1[3]);  // AND_Gate
  and and_4 (and_4_out, ~in_1[0], in_1[1], in_1[3]);  // AND_Gate
  or or_1 (out_2, and_1_out, and_2_out, and_3_out, and_4_out);
endmodule

module ALUop1 (
  input  [3:0] in_1,
  output out_2
);

  wire and_1_out, and_2_out;

  and and_1 (and_1_out, ~in_1[0], ~in_1[1], ~in_1[2], in_1[3]);  // AND_Gate
  and and_2 (and_2_out, in_1[1], ~in_1[2], in_1[3]);  // AND_Gate
  or or_1 (out_2, and_1_out, and_2_out);
endmodule

module ALUop2 (
  input  [3:0] in_1,
  output out_2
);

  wire and_1_out, and_2_out, and_3_out;

  and and_1 (and_1_out, ~in_1[1], ~in_1[2], in_1[3]);  // AND_Gate
  and and_2 (and_2_out, ~in_1[1], ~in_1[2], ~in_1[3], in_1[0]);  // AND_Gate
  and and_3 (and_3_out, in_1[1], ~in_1[2], ~in_1[3]);  // AND_Gate
  or or_1 (out_2, and_1_out, and_2_out, and_3_out);
endmodule

module ALUSrc (
  input  [3:0] in_1,
  output out_2
);

  wire and_1_out, and_2_out, and_3_out;

  and and_1 (and_1_out, ~in_1[0], ~in_1[1], ~in_1[3]);  // AND_Gate
  and and_2 (and_2_out, in_1[3], ~in_1[2], ~in_1[1]);  // AND_Gate
  and and_3 (and_3_out, in_1[0], in_1[2], ~in_1[3]);  // AND_Gate
  or or_1 (out_2, and_1_out, and_2_out, and_3_out);
endmodule

module test (
);

  Control control_1 ();  // open: in_1, out_2, Mem_Write, Clock_Stop, Write_ra, Read_ra, Reg_Write, Branch, ALU_op1, ALU_op2, ALU_Src, out_3, out_13
endmodule

module CPU (
);

  wire and_1_out, clock_1_out, control_1_alu_op1, control_1_alu_op2, control_1_alu_src, control_1_branch,
       control_1_clock_stop, control_1_mem_write, control_1_out_2, control_1_out_3, control_1_out_13,
       control_1_read_ra, control_1_reg_write, control_1_write_ra, not_1_out;
  wire [2:0] multiplexer_2_out, multiplexer_3_out, undriven;
  wire [15:0] adder_1_out, adder_2_out, bit_extender_1_out, multiplexer_1_out, multiplexer_4_out,
       multiplexer_5_out, multiplexer_6_out, ram_1_data, ram_2_data, register_1_q, register_2_q,
       registers_1_data1, registers_1_data2, shifter_1_out, undriven_2;

  Clock clock_1 (.out(clock_1_out));
  and and_1 (and_1_out, clock_1_out, not_1_out);
  not not_1 (not_1_out, control_1_clock_stop);
  Register #(.width(16)) register_1 (.D(multiplexer_5_out), .Q(register_1_q), .clk(and_1_out));  // open: en, clr
  Register #(.width(16)) register_2 (
    .D(multiplexer_5_out), .en(control_1_write_ra), .Q(register_2_q), .clk(and_1_out));  // open: clr
  Multiplexer #(.width(16), .enable("false")) multiplexer_1 (
    .in0(register_1_q), .in1(register_2_q), .out(multiplexer_1_out), .sel(control_1_read_ra));
  RAM #(.addrWidth(16), .dataWidth(16)) ram_1 (.addr(multiplexer_1_out), .data(ram_1_data));  // open: sel, clk, ld, clr
  Adder #(.width(16)) adder_1 (.a(16'h4), .b(register_1_q), .out(adder_1_out));  // open: cin, cout
  Control control_1 (
    .in_1(ram_1_data[15:12]), .out_2(control_1_out_2), .Mem_Write(control_1_mem_write),
    .Clock_Stop(control_1_clock_stop), .Write_ra(control_1_write_ra), .Read_ra(control_1_read_ra),
    .Reg_Write(control_1_reg_write), .Branch(control_1_branch), .ALU_op1(control_1_alu_op1),
    .ALU_op2(control_1_alu_op2), .ALU_Src(control_1_alu_src), .out_3(control_1_out_3),
    .out_13(control_1_out_13));
  Multiplexer #(.width(3), .enable("false")) multiplexer_2 (
    .in0(ram_1_data[5:3]), .in1(ram_1_data[8:6]), .out(multiplexer_2_out), .sel(control_1_out_13));
  Multiplexer #(.width(3), .enable("false")) multiplexer_3 (
    .in0(ram_1_data[8:6]), .in1(ram_1_data[11:9]), .out(multiplexer_3_out), .sel(control_1_out_13));
  Registers registers_1 (
    .Write(control_1_reg_write), .Write_Register(undriven), .Register_Data(multiplexer_6_out),
    .writeRegister(and_1_out), .Data2(registers_1_data2), .Read_Regisiter2(multiplexer_3_out),
    .Read_Regisiter1(multiplexer_2_out), .Data1(registers_1_data1));  // open: reset
  assign bit_extender_1_out = {{13{1'b0}}, ram_1_data[2:0]};  // Bit_Extender bit_extender_1
  Multiplexer #(.width(16), .enable("false")) multiplexer_4 (
    .in0(registers_1_data2), .in1(bit_extender_1_out), .out(multiplexer_4_out), .sel(control_1_alu_src));
  Shifter #(.width(16)) shifter_1 (.in(bit_extender_1_out), .\dist (4'b0010), .out(shifter_1_out));
  Adder #(.width(16)) adder_2 (.a(adder_1_out), .b(shifter_1_out), .out(adder_2_out));  // open: cin, cout
  Multiplexer #(.width(16), .enable("false")) multiplexer_5 (
    .in0(adder_1_out), .in1(adder_2_out), .out(multiplexer_5_out));  // open: sel
  RAM #(.addrWidth(16), .dataWidth(16)) ram_2 (
    .addr(undriven_2), .data(ram_2_data), .sel(control_1_mem_write), .ld(control_1_out_2));  // open: clk, clr
  Multiplexer #(.width(16), .enable("false")) multiplexer_6 (
    .in0(ram_2_data), .in1(undriven_2), .out(multiplexer_6_out), .sel(control_1_out_3));
endmodule

module regDst (
  input  [3:0] in_1,
  output out_2
);

  wire or_1_out;

  or or_1 (or_1_out, ~in_1[2], ~in_1[1]);  // OR_Gate
  // AND_Gate and_1 is placed but not wired
  and and_2 (out_2, ~in_1[0], ~in_1[3], or_1_out);  // AND_Gate
endmodule

module Registers (
  input  Write,
  input  [2:0] Write_Register,
  input  [2:0] Read_Regisiter2,
  input  [2:0] Read_Regisiter1,
  input  [15:0] Register_Data,
  input  writeRegister,
  input  reset,
  output [15:0] Data1,
  output [15:0] Data2
);

  wire and_1_out, and_2_out, and_3_out, and_4_out, and_5_out, and_6_out, and_7_out, and_8_out,
       decoder_1_out0, decoder_1_out1, decoder_1_out2, decoder_1_out3, decoder_1_out4, decoder_1_out5,
       decoder_1_out6, decoder_1_out7;
  wire [15:0] r1_q, r2_q, r3_q, r4_q, r5_q, r6_q, r7_q, r8_q;

  Decoder #(.select(3), .enable("false")) decoder_1 (
    .out0(decoder_1_out0), .out1(decoder_1_out1), .out2(decoder_1_out2), .out3(decoder_1_out3),
    .out4(decoder_1_out4), .out5(decoder_1_out5), .out6(decoder_1_out6), .out7(decoder_1_out7),
    .sel(Write_Register));
  and and_1 (and_1_out, Write, decoder_1_out0);
  and and_2 (and_2_out, Write, decoder_1_out1);
  and and_3 (and_3_out, Write, decoder_1_out2);
  and and_4 (and_4_out, Write, decoder_1_out3);
  and and_5 (and_5_out, Write, decoder_1_out4);
  and and_6 (and_6_out, Write, decoder_1_out5);
  and and_7 (and_7_out, Write, decoder_1_out6);
  and and_8 (and_8_out, Write, decoder_1_out7);
  Register #(.width(16)) r1 (.D(Register_Data), .en(and_1_out), .Q(r1_q), .clk(writeRegister), .clr(reset));
  Register #(.width(16)) r2 (.D(Register_Data), .en(and_2_out), .Q(r2_q), .clk(writeRegister), .clr(reset));
  Register #(.width(16)) r3 (.D(Register_Data), .en(and_3_out), .Q(r3_q), .clk(writeRegister), .clr(reset));
  Register #(.width(16)) r4 (.D(Register_Data), .en(and_4_out), .Q(r4_q), .clk(writeRegister), .clr(reset));
  Register #(.width(16)) r5 (.en(and_5_out), .Q(r5_q), .clk(writeRegister), .clr(reset));  // open: D
  Register #(.width(16)) r6 (.en(and_6_out), .Q(r6_q), .clk(writeRegister), .clr(reset));  // open: D
  Register #(.width(16)) r7 (.en(and_7_out), .Q(r7_q), .clk(writeRegister), .clr(reset));  // open: D
  Register #(.width(16)) r8 (.en(and_8_out), .Q(r8_q), .clk(writeRegister), .clr(reset));  // open: D
  Multiplexer #(.select(3), .width(16), .enable("false")) multiplexer_1 (
    .in0(r1_q), .in1(r2_q), .in2(r3_q), .in3(r4_q), .in4(r5_q), .in5(r6_q), .in6(r7_q), .in7(r8_q),
    .out(Data1), .sel(Read_Regisiter1));
  Multiplexer #(.select(3), .width(16), .enable("false")) multiplexer_2 (
    .in0(r1_q), .in1(r2_q), .in2(r3_q), .in3(r4_q), .in4(r5_q), .in5(r6_q), .in6(r7_q), .in7(r8_q),
    .out(Data2), .sel(Read_Regisiter2));
endmodule
