// Logisim project CPU_Control_evolution.circ as structural Verilog: 20 circuits, main circuit Control
module Control (
  input  [3:0] in_1,
  output out_2,
  output out_3,
  output Mem_Write,
  output Clock_Stop,
  output Write_ra,
  output Read_ra,
  output Reg_Write,
  output ALU_op1,
  output ALU_op2,
  output ALU_Src,
  output REG_Dst,
  output out_13,
  output [1:0] Branch
);

  MemRead memread_1 (.in_1(in_1), .out_2(out_2));
  MemtoReg memtoreg_1 (.in_1(in_1), .out_2(out_3));
  MemWrite memwrite_1 (.in_1(in_1), .out_2(Mem_Write));
  clockStop clockstop_1 (.in_1(in_1), .out_2(Clock_Stop));
  writea_ra_88f6a453 writea_ra_88f6a453_1 (.in_1(in_1), .out_2(Write_ra));
  Read_ra_223be093 read_ra_223be093_1 (.in_1(in_1), .out_2(Read_ra));
  RegWrite regwrite_1 (.in_1(in_1), .out_2(Reg_Write));
  ALUop1 aluop1_1 (.in_1(in_1), .out_2(ALU_op1));
  ALUop2 aluop2_1 (.in_1(in_1), .out_2(ALU_op2));
  ALUSrc alusrc_1 (.in_1(in_1), .out_2(ALU_Src));
  regDst regdst_1 (.out_2(REG_Dst), .in_1(in_1));
  ALUBranch alubranch_1 (.in_1(in_1), .out_2(out_13));
  Branch_2 branch_2_1 (.in_1(in_1), .out_2(Branch[0]));
  Branch_1 branch_1_1 (.in_1(in_1), .out_2(Branch[1]));
endmodule

module MemRead (
  input  [3:0] in_1,
  output out_2
);

  wire not_1_out, not_2_out, not_3_out;

  not not_1 (not_1_out, in_1[1]);
  not not_2 (not_2_out, in_1[2]);
  not not_3 (not_3_out, in_1[3]);
  // AND_Gate and_1 has open pins: in0=in_1[0], in1=not_1_out, in2=not_2_out, in3=not_3_out, out=open

  assign out_2 = 1'b1;
endmodule

// Mem_to_Reg
module MemtoReg (
  input  [3:0] in_1,
  output out_2
);

  wire not_1_out, not_2_out, not_3_out;

  not not_1 (not_1_out, in_1[0]);
  not not_2 (not_2_out, in_1[1]);
  not not_3 (not_3_out, in_1[3]);
  and and_1 (out_2, not_1_out, not_2_out, in_1[2], not_3_out);
endmodule

module MemWrite (
  input  [3:0] in_1,
  output out_2
);

  wire not_1_out, not_2_out;

  not not_1 (not_1_out, in_1[1]);
  not not_2 (not_2_out, in_1[3]);
  and and_1 (out_2, in_1[0], not_1_out, in_1[2], not_2_out);
endmodule

module clockStop (
  input  [3:0] in_1,
  output out_2
);

  and and_1 (out_2, in_1[0], in_1[1], in_1[2], in_1[3]);
endmodule

module writea_ra_88f6a453 (
  input  [3:0] in_1,
  output out_2
);

  wire not_1_out;

  not not_1 (not_1_out, in_1[1]);
  and and_1 (out_2, in_1[0], not_1_out, in_1[2], in_1[3]);
endmodule

module Read_ra_223be093 (
  input  [3:0] in_1,
  output out_2
);

  wire not_1_out;

  not not_1 (not_1_out, in_1[0]);
  and and_1 (out_2, not_1_out, in_1[1], in_1[2], in_1[3]);
endmodule

module RegWrite (
  input  [3:0] in_1,
  output out_2
);

  wire and_1_out, and_2_out, and_3_out, and_4_out;

  and and_1 (and_1_out, ~in_1[0], ~in_1[1], ~in_1[3]);  // AND_Gate
  and and_2 (and_2_out, ~in_1[3], ~in_1[2], ~in_1[1]);  // AND_Gate
  and and_3 (and_3_out, in_1[3], ~in_1[2], ~in_1[1]);  // AND_Gate
  and and_4 (and_4_out, in_1[1], ~in_1[3]);  // AND_Gate
  or or_1 (out_2, and_1_out, and_2_out, and_3_out, and_4_out);
endmodule

module Branch_1 (
  input  [3:0] in_1,
  output out_2
);

  wire and_1_out, and_2_out;

  and and_1 (and_1_out, in_1[0], ~in_1[1], in_1[2], in_1[3]);  // AND_Gate
  and and_2 (and_2_out, ~in_1[0], in_1[1], in_1[2], in_1[3]);  // AND_Gate
  or or_1 (out_2, and_1_out, and_2_out);
endmodule

module ALUop1 (
  input  [3:0] in_1,
  output out_2
);

  wire and_1_out, and_2_out, and_3_out;

  and and_1 (and_1_out, ~in_1[0], ~in_1[1], in_1[2], ~in_1[3]);  // AND_Gate
  and and_2 (and_2_out, in_1[0], ~in_1[1], ~in_1[2], in_1[3]);  // AND_Gate
  and and_3 (and_3_out, in_1[0], ~in_1[3]);  // AND_Gate
  or or_1 (out_2, and_1_out, and_2_out, and_3_out);
endmodule

module ALUop2 (
  input  [3:0] in_1,
  output out_2
);

  wire and_1_out, and_2_out;

  and and_1 (and_1_out, ~in_1[1], ~in_1[2], in_1[3]);  // AND_Gate
  and and_2 (and_2_out, in_1[1], ~in_1[2], ~in_1[3]);  // AND_Gate
  or or_1 (out_2, and_1_out, and_2_out);
endmodule

module ALUSrc (
  input  [3:0] in_1,
  output out_2
);

  wire and_1_out, and_2_out, and_3_out;

  and and_1 (and_1_out, ~in_1[0], ~in_1[1], ~in_1[3]);  // AND_Gate
  and and_2 (and_2_out, in_1[3], ~in_1[2], ~in_1[1]);  // AND_Gate
  and and_3 (and_3_out, in_1[0], in_1[2], ~in_1[3]);  // AND_Gate
  or or_1 (out_2, and_1_out, and_2_out, and_3_out);
endmodule

module test (
);

  Control control_1 ();  // open: out_3, Mem_Write, Clock_Stop, Write_ra, Read_ra, Reg_Write, ALU_op1, ALU_op2, ALU_Src, out_2, out_13, REG_Dst, Branch, in_1
endmodule

module CPU (
);

  wire alu_1_zero, and_1_out, clock_1_out, control_1_alu_src, control_1_clock_stop, control_1_mem_write,
       control_1_out_2, control_1_out_3, control_1_out_13, control_1_read_ra, control_1_reg_dst,
       control_1_reg_write, control_1_write_ra, not_1_out;
  wire [1:0] control_1_alu_op1, control_1_branch;
  wire [2:0] multiplexer_1_out, multiplexer_2_out, multiplexer_3_out;
  wire [15:0] adder_1_out, adder_2_out, adder_3_out, alu_1_alures, bit_extender_1_out, multiplexer_4_out,
       multiplexer_5_out, multiplexer_6_out, PC_q, ra_q, ram_1_dout, ram_2_dout, registers_1_data1,
       registers_1_data2, shifter_1_out;

  Clock clock_1 (.out(clock_1_out));
  and and_1 (and_1_out, clock_1_out, not_1_out);
  not not_1 (not_1_out, control_1_clock_stop);
  Register #(.trigger("falling"), .width(16)) PC (
    .D(multiplexer_5_out), .en(1'b1), .Q(PC_q), .clk(and_1_out));  // open: clr
  Register #(.trigger("falling"), .width(16)) ra (
    .D(multiplexer_5_out), .en(control_1_write_ra), .Q(ra_q), .clk(and_1_out));  // open: clr
  RAM #(.addrWidth(16), .dataWidth(16), .enables("line"), .trigger("falling"), .\type ("nonvolatile")) ram_1 (
    .addr(PC_q), .clk(and_1_out), .dout(ram_1_dout));  // open: we, din
  // Probe on ram_1_dout[11:9]
  // Probe on ram_1_dout[8:6]
  // Probe on ram_1_dout[5:3]
  // Probe on ram_1_dout[2:0]
  Adder #(.width(16)) adder_1 (.a(16'h1), .b(PC_q), .out(adder_1_out));  // open: cin, cout
  // Probe on ram_1_dout[15:12]
  Control control_1 (
    .out_3(control_1_out_3), .Mem_Write(control_1_mem_write), .Clock_Stop(control_1_clock_stop),
    .Write_ra(control_1_write_ra), .Read_ra(control_1_read_ra), .Reg_Write(control_1_reg_write),
    .ALU_op1(control_1_alu_op1[0]), .ALU_op2(control_1_alu_op1[1]), .ALU_Src(control_1_alu_src),
    .out_2(control_1_out_2), .out_13(control_1_out_13), .REG_Dst(control_1_reg_dst),
    .Branch(control_1_branch), .in_1(ram_1_dout[15:12]));
  Multiplexer #(.enable("false"), .width(3)) multiplexer_1 (
    .in0(ram_1_dout[11:9]), .in1(ram_1_dout[8:6]), .out(multiplexer_1_out), .sel(control_1_reg_dst));
  Multiplexer #(.enable("false"), .width(3)) multiplexer_2 (
    .in0(ram_1_dout[8:6]), .in1(ram_1_dout[5:3]), .out(multiplexer_2_out), .sel(control_1_reg_dst));
  Multiplexer #(.enable("false"), .width(3)) multiplexer_3 (
    .in0(ram_1_dout[8:6]), .in1(ram_1_dout[2:0]), .out(multiplexer_3_out), .sel(control_1_reg_dst));
  // Probe on ram_1_dout[5:0]
  // Probe on multiplexer_1_out
  // Probe on multiplexer_2_out
  // Probe on multiplexer_3_out
  Registers registers_1 (
    .Data1(registers_1_data1), .Data2(registers_1_data2), .Write_Register(multiplexer_3_out),
    .Write(control_1_reg_write), .Register_Data(multiplexer_6_out), .clock(and_1_out),
    .Read_Regisiter2(multiplexer_2_out), .Read_Regisiter1(multiplexer_1_out));  // open: reset
  assign bit_extender_1_out = {{10{ram_1_dout[5]}}, ram_1_dout[5:0]};  // Bit_Extender bit_extender_1
  // Probe on registers_1_data1
  Multiplexer #(.enable("false"), .width(16)) multiplexer_4 (
    .in0(registers_1_data2), .in1(bit_extender_1_out), .out(multiplexer_4_out), .sel(control_1_alu_src));
  // Probe on multiplexer_4_out
  // Probe on multiplexer_6_out
  Shifter #(.width(16)) shifter_1 (.in(bit_extender_1_out), .\dist (4'b0001), .out(shifter_1_out));
  // Probe on control_1_alu_op1
  Adder #(.width(16)) adder_2 (.a(adder_1_out), .b(shifter_1_out), .out(adder_2_out));  // open: cin, cout
  ALU alu_1 (
    .ALURes(alu_1_alures), .ZERO(alu_1_zero), .Data1(registers_1_data1), .Data2(multiplexer_4_out),
    .ALUOp(control_1_alu_op1), .ALUBranch(control_1_out_13));
  Adder #(.width(16)) adder_3 (.a(bit_extender_1_out), .b(adder_1_out), .out(adder_3_out));  // open: cin, cout
  // AND_Gate and_2 has open pins: in0=alu_1_zero, out=open
  RAM #(.addrWidth(16), .dataWidth(16)) ram_2 (
    .addr(alu_1_alures), .we(control_1_mem_write), .oe(control_1_out_2), .clk(and_1_out),
    .din(registers_1_data2), .dout(ram_2_dout));
  // Probe on alu_1_alures
  Multiplexer #(.enable("false"), .select(2), .width(16)) multiplexer_5 (
    .in0(adder_1_out), .in1(adder_2_out), .in2(ra_q), .in3(adder_3_out), .out(multiplexer_5_out),
    .sel(control_1_branch));
  // Probe on alu_1_alures
  // Probe on ram_2_dout
  Multiplexer #(.enable("false"), .width(16)) multiplexer_6 (
    .in0(alu_1_alures), .in1(ram_2_dout), .out(multiplexer_6_out), .sel(control_1_out_3));

  // Notes on the sheet:
  //   immediate number
  //   rs
  //   rt
  //   rd
endmodule

module regDst (
  input  [3:0] in_1,
  output out_2
);

  wire and_1_out, and_2_out;

  and and_1 (and_1_out, ~in_1[3], ~in_1[2], in_1[0]);  // AND_Gate
  and and_2 (and_2_out, ~in_1[3], in_1[1], ~in_1[0]);  // AND_Gate
  or or_1 (out_2, and_1_out, and_2_out);
endmodule

module Registers (
  input  Write,
  input  [2:0] Write_Register,
  input  [2:0] Read_Regisiter2,
  input  [2:0] Read_Regisiter1,
  input  [15:0] Register_Data,
  input  clock,
  input  reset,
  output [15:0] Data1,
  output [15:0] Data2
);

  wire and_1_out, and_2_out, and_3_out, and_4_out, and_5_out, and_6_out, and_7_out, and_8_out,
       decoder_1_out0, decoder_1_out1, decoder_1_out2, decoder_1_out3, decoder_1_out4, decoder_1_out5,
       decoder_1_out6, decoder_1_out7;
  wire [15:0] r1_q, r2_q, r3_q, r4_q, r5_q, r6_q, r7_q, r8_q;

  Decoder #(.enable("false"), .select(3)) decoder_1 (
    .out0(decoder_1_out0), .out1(decoder_1_out1), .out2(decoder_1_out2), .out3(decoder_1_out3),
    .out4(decoder_1_out4), .out5(decoder_1_out5), .out6(decoder_1_out6), .out7(decoder_1_out7),
    .sel(Write_Register));
  and and_1 (and_1_out, Write, decoder_1_out0);
  and and_2 (and_2_out, Write, decoder_1_out1);
  and and_3 (and_3_out, Write, decoder_1_out2);
  and and_4 (and_4_out, Write, decoder_1_out3);
  and and_5 (and_5_out, Write, decoder_1_out4);
  and and_6 (and_6_out, Write, decoder_1_out5);
  and and_7 (and_7_out, Write, decoder_1_out6);
  and and_8 (and_8_out, Write, decoder_1_out7);
  Register #(.trigger("falling"), .width(16)) r1 (
    .D(Register_Data), .en(and_1_out), .Q(r1_q), .clk(clock), .clr(reset));
  Register #(.trigger("falling"), .width(16)) r2 (
    .D(Register_Data), .en(and_2_out), .Q(r2_q), .clk(clock), .clr(reset));
  Register #(.trigger("falling"), .width(16)) r3 (
    .D(Register_Data), .en(and_3_out), .Q(r3_q), .clk(clock), .clr(reset));
  Register #(.trigger("falling"), .width(16)) r4 (
    .D(Register_Data), .en(and_4_out), .Q(r4_q), .clk(clock), .clr(reset));
  Register #(.trigger("falling"), .width(16)) r5 (
    .D(Register_Data), .en(and_5_out), .Q(r5_q), .clk(clock), .clr(reset));
  Register #(.trigger("falling"), .width(16)) r6 (
    .D(Register_Data), .en(and_6_out), .Q(r6_q), .clk(clock), .clr(reset));
  Register #(.trigger("falling"), .width(16)) r7 (
    .D(Register_Data), .en(and_7_out), .Q(r7_q), .clk(clock), .clr(reset));
  Register #(.trigger("falling"), .width(16)) r8 (
    .D(Register_Data), .en(and_8_out), .Q(r8_q), .clk(clock), .clr(reset));
  Multiplexer #(.enable("false"), .select(3), .width(16)) multiplexer_1 (
    .in0(r1_q), .in1(r2_q), .in2(r3_q), .in3(r4_q), .in4(r5_q), .in5(r6_q), .in6(r7_q), .in7(r8_q),
    .out(Data1), .sel(Read_Regisiter1));
  Multiplexer #(.enable("false"), .select(3), .width(16)) multiplexer_2 (
    .in0(r1_q), .in1(r2_q), .in2(r3_q), .in3(r4_q), .in4(r5_q), .in5(r6_q), .in6(r7_q), .in7(r8_q),
    .out(Data2), .sel(Read_Regisiter2));
endmodule

module ALU (
  input  [15:0] Data1,
  input  ALUBranch,
  input  [15:0] Data2,
  input  [1:0] ALUOp,
  output ZERO,
  output [15:0] ALURes
);

  wire BLE_out, BNE_out, comparator_1_eq, comparator_1_lt;
  wire [15:0] adder_1_out, and_1_out, or_1_out;

  Comparator #(.width(16)) comparator_1 (.a(Data1), .b(Data2), .eq(comparator_1_eq), .lt(comparator_1_lt));  // open: gt
  Adder #(.width(16)) adder_1 (.a(Data1), .b(Data2), .out(adder_1_out));  // open: cin, cout
  assign and_1_out = Data1 & Data2;  // AND_Gate and_1, 16 bits wide
  assign or_1_out = Data1 | Data2;  // OR_Gate or_1, 16 bits wide
  or BLE (BLE_out, comparator_1_eq, comparator_1_lt);
  not BNE (BNE_out, comparator_1_eq);
  // Probe on adder_1_out
  // Probe on and_1_out
  // Probe on or_1_out
  Multiplexer multiplexer_1 (.in0(BLE_out), .in1(BNE_out), .out(ZERO), .sel(ALUBranch));  // open: en
  Multiplexer #(.select(2), .width(16)) multiplexer_2 (
    .in0(Data2), .in1(adder_1_out), .in2(and_1_out), .in3(or_1_out), .out(ALURes), .sel(ALUOp));  // open: en
endmodule

module ALUBranch (
  input  [3:0] in_1,
  output out_2
);

  and and_1 (out_2, in_1[0], in_1[1], ~in_1[2], in_1[3]);  // AND_Gate
endmodule

module BranchArchive (
  input  [3:0] in_1,
  output out_2
);

  wire and_1_out, and_2_out, and_3_out, and_4_out;

  and and_1 (and_1_out, in_1[2], ~in_1[1], ~in_1[0]);  // AND_Gate
  and and_2 (and_2_out, ~in_1[1], in_1[2], in_1[3]);  // AND_Gate
  and and_3 (and_3_out, in_1[1], ~in_1[2], in_1[3]);  // AND_Gate
  and and_4 (and_4_out, ~in_1[0], in_1[1], in_1[3]);  // AND_Gate
  or or_1 (out_2, and_1_out, and_2_out, and_3_out, and_4_out);
endmodule

module Branch_2 (
  input  [3:0] in_1,
  output out_2
);

  wire and_1_out, and_2_out;

  and and_1 (and_1_out, ~in_1[1], in_1[2], in_1[3]);  // AND_Gate
  and and_2 (and_2_out, in_1[1], ~in_1[2], in_1[3]);  // AND_Gate
  or or_1 (out_2, and_1_out, and_2_out);
endmodule
