// Logisim project cpu_57883349.circ as structural Verilog: 4 circuits, main circuit CPU
module CPU (
  input  [15:0] in_1,
  input  in_2,
  input  in_3
);

  wire and_1_out, clock_1_out;
  wire [15:0] adder_1_out, register_1_q;

  Clock clock_1 (.out(clock_1_out));
  buf and_1 (and_1_out, clock_1_out);  // AND_Gate
  Register #(.width(16)) register_1 (.D(adder_1_out), .en(in_2), .Q(register_1_q), .clk(and_1_out));  // open: clr
  Adder #(.width(16)) adder_1 (.a(in_1), .b(register_1_q), .out(adder_1_out));  // open: cin, cout
  ROM #(.addrWidth(16), .dataWidth(16)) rom_1 (.addr(register_1_q), .sel(in_3));  // open: data
endmodule

module ControlUnit (
  input  in_1,
  input  in_2
);
endmodule

module Registers (
  input  Write,
  input  [2:0] Write_Register,
  input  [2:0] Read_Regisiter2,
  input  [2:0] Read_Regisiter1,
  input  [15:0] Register_Data,
  input  writeRegister,
  input  reset,
  output [15:0] Data2
);

  wire and_1_out, and_2_out, and_3_out, and_4_out, and_5_out, and_6_out, and_7_out, and_8_out,
       decoder_1_out0, decoder_1_out1, decoder_1_out2, decoder_1_out3, decoder_1_out4, decoder_1_out5,
       decoder_1_out6, decoder_1_out7;
  wire [15:0] r1_q, r2_q, r3_q, r4_q, r5_q, r6_q, r7_q, r8_q;

  Decoder #(.select(3), .enable("false")) decoder_1 (
    .out0(decoder_1_out0), .out1(decoder_1_out1), .out2(decoder_1_out2), .out3(decoder_1_out3),
    .out4(decoder_1_out4), .out5(decoder_1_out5), .out6(decoder_1_out6), .out7(decoder_1_out7),
    .sel(Write_Register));
  and and_1 (and_1_out, Write, decoder_1_out0);
  and and_2 (and_2_out, Write, decoder_1_out1);
  and and_3 (and_3_out, Write, decoder_1_out2);
  and and_4 (and_4_out, Write, decoder_1_out3);
  and and_5 (and_5_out, Write, decoder_1_out4);
  and and_6 (and_6_out, Write, decoder_1_out5);
  and and_7 (and_7_out, Write, decoder_1_out6);
  and and_8 (and_8_out, Write, decoder_1_out7);
  Register #(.width(16)) r1 (.D(Register_Data), .en(and_1_out), .Q(r1_q), .clk(writeRegister), .clr(reset));
  Register #(.width(16)) r2 (.D(Register_Data), .en(and_2_out), .Q(r2_q), .clk(writeRegister), .clr(reset));
  Register #(.width(16)) r3 (.D(Register_Data), .en(and_3_out), .Q(r3_q), .clk(writeRegister), .clr(reset));
  Register #(.width(16)) r4 (.D(Register_Data), .en(and_4_out), .Q(r4_q), .clk(writeRegister), .clr(reset));
  Register #(.width(16)) r5 (.en(and_5_out), .Q(r5_q), .clk(writeRegister), .clr(reset));  // open: D
  Register #(.width(16)) r6 (.en(and_6_out), .Q(r6_q), .clk(writeRegister), .clr(reset));  // open: D
  Register #(.width(16)) r7 (.en(and_7_out), .Q(r7_q), .clk(writeRegister), .clr(reset));  // open: D
  Register #(.width(16)) r8 (.en(and_8_out), .Q(r8_q), .clk(writeRegister), .clr(reset));  // open: D
  Multiplexer #(.select(3), .width(16), .enable("false")) multiplexer_1 (
    .in0(r1_q), .in1(r2_q), .in2(r3_q), .in3(r4_q), .in4(r5_q), .in5(r6_q), .in6(r7_q), .in7(r8_q),
    .sel(Read_Regisiter1));  // open: out
  Multiplexer #(.select(3), .width(16), .enable("false")) multiplexer_2 (
    .in0(r1_q), .in1(r2_q), .in2(r3_q), .in3(r4_q), .in4(r5_q), .in5(r6_q), .in6(r7_q), .in7(r8_q),
    .out(Data2), .sel(Read_Regisiter2));
endmodule

module ALU (
  input  [15:0] in_1,
  input  in_2,
  input  [15:0] in_3,
  input  [1:0] in_4,
  output out_5,
  output [15:0] out_6
);

  wire BLE_out, BNE_out, comparator_1_eq, comparator_1_lt;
  wire [15:0] adder_1_out, and_1_out, or_1_out;

  Comparator #(.width(16), .mode(16)) comparator_1 (
    .a(in_1), .b(in_3), .eq(comparator_1_eq), .lt(comparator_1_lt));  // open: gt
  Adder #(.width(16)) adder_1 (.a(in_1), .b(in_3), .out(adder_1_out));  // open: cin, cout
  assign and_1_out = in_1 & in_3;  // AND_Gate and_1, 16 bits wide
  assign or_1_out = in_1 | in_3;  // OR_Gate or_1, 16 bits wide
  or BLE (BLE_out, comparator_1_eq, comparator_1_lt);
  not BNE (BNE_out, comparator_1_eq);
  Multiplexer multiplexer_1 (.in0(BLE_out), .in1(BNE_out), .out(out_5), .sel(in_2));  // open: en
  Multiplexer #(.select(2), .width(16)) multiplexer_2 (
    .in0({16{1'b0}}), .in1(adder_1_out), .in2(and_1_out), .in3(or_1_out), .out(out_6), .sel(in_4));  // open: en
endmodule
